# Fritzing sketch circuit (saved by Fritzing 0.9.3b)
perfboards: 1

parts:
  Part2 = Adafruit Pi Cobbler Plus [part_number="Adafruit #2029"]
  Pololu_A1 = Pololu A4988 [package=SO16]
  Pololu_A2 = Pololu A4988 [package=SO16]
  IC1 = Voltage Regulator [package=78xxl]  # not connected
  C2 = Electrolytic Capacitor [capacitance=47µF package="0605 [SMD, electrolytic]"]  # not connected
  C3 = Electrolytic Capacitor [capacitance=47µF package="0605 [SMD, electrolytic]"]  # not connected
  R1 = Resistor [tolerance=±5% resistance=1k package="2512 [SMD]"]
  J6 = Power Jack [package=power_jack_smd]  # not connected

nets:
  VDD: Part2.+3.3V, Pololu_A1.VDD, Pololu_A2.VDD
  N1: Part2.GPIO23, R1.Pin_0
  N2: Part2.GPIO25, Pololu_A2.ENABLE
  N3: Part2.CE0, Pololu_A2.SLEEP
  N4: Part2.CE1, Pololu_A2.STEP
  N5: Part2.EECLK, Pololu_A2.DIR
  N6: Part2.GPIO12, Pololu_A1.ENABLE
  N7: Part2.GPIO16, Pololu_A1.SLEEP
  N8: Part2.GPIO20, Pololu_A1.STEP
  N9: Part2.GPIO21, Pololu_A1.DIR
  N10: Pololu_A1.VMOT, Pololu_A2.VMOT

custom parts:
  Adafruit Pi Cobbler Plus: The Raspberry Pi B+/Pi 2/ Pi 3 has landed on the Maker World like a 40-GPIO pinned, quad-USB ported, credit card sized bomb of DIY joy. And while you can use most of our great Model B accessories by hooking up our downgrade cable, its probably a good time to upgrade your set up and accessorize using all of the Model B+'s / Pi 2's / Pi 3's 40 pins. That's why we now carry the Adafruit Assembled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
